# Fritzing sketch whitecane (saved by Fritzing 0.9.2b)
breadboards: 1

parts:
  Part1 = PowerBoost 500 Charger
  Teensy_3_1 = Teensy 3.1  # not connected
  R1 = Resistor [tolerance=±5% resistance=220 package=THT]  # not connected
  R2 = Resistor [tolerance=±5% resistance=320 package=THT]  # not connected
  U1 = SWITCH_SPDT [package=kps-1290]
  C1 = Electrolytic Capacitor [capacitance=1000μF package="1010 [SMD, electrolytic]"]  # not connected
  C2 = Electrolytic Capacitor [capacitance=1000μF package="1010 [SMD, electrolytic]"]  # not connected
  Q1 = Basic FET N-Channel [package="D2Pak [SMD]"]  # not connected

nets:
  N1: Part1.ENABLE, U1.O
  N2: Part1.GND, U1.P
  N3: Part1.LBO, U1.S

custom parts:
  PowerBoost 500 Charger: The PowerBoost 500C is a little DC/DC boost converter module that can be powered by any 3.7V LiIon/LiPoly battery, and convert the battery output to 5.2V DC for running your 5V projects. At its heart is a TPS61090 boost converter from TI. This boost converter chip has some really nice extras such as low battery detection, 2A internal switch, synchronous conversion, excellent efficiency, and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
